# Fritzing sketch Pico_potentiometerLED (saved by Fritzing 0.9.3b)
breadboards: 1

parts:
  Mod1 = Raspberry Pi Pico
  R1 = Resistor [tolerance=±5% resistance=220 package=THT]
  LED1 = LED - 5mm [color="Red (633nm)" package="5 mm [THT]"]
  R2 = Rotary Potentiometer (Small) [maximum_resistance=100kΩ package=THT]

nets:
  N1: Mod1.pin_2, Mod1.pin_27
  N2: Mod1.pin_3, Mod1.pin_5, Mod1.pin_6, Mod1.pin_7, Mod1.pin_8, Mod1.pin_12, Mod1.pin_13, Mod1.pin_16, Mod1.pin_17, Mod1.pin_18, Mod1.pin_22, Mod1.pin_23, Mod1.pin_24, Mod1.pin_26, Mod1.pin_28, Mod1.pin_32, Mod1.pin_33, Mod1.pin_38, Mod1.pin_42, R1.Pin_0, R2.leg1, R2.leg2
  N3: Mod1.pin_4, Mod1.pin_29, Mod1.pin_31, R2.wiper
  N4: R1.Pin_1, LED1.anode

custom parts:
  Raspberry Pi Pico: Raspberry Pi Pico. Based around the RP2040 microcontroller the Pico is a low cost microcontroller device bringing Raspberry Pi quality, cost, and easy of use to the microcontroller space. Jan 2021, Split part in to two versions: tht (this one) and SMD. This one will drill holes for a .1 in header in pcb to allow plugging in the module as well as providing pads to solder the module to the top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
